# Fritzing sketch victoria (saved by Fritzing 0.9.2b)
circuit board: 8.46667cm x 5.64444cm
breadboards: 2

parts:
  Part1 = Arduino Mega 2560 (Rev3)
  Q1 = MOSFET-NCHANNEL [package=to-92]
  DS2 = DS18B20 1-Wire Temperature Sensor [part_number=DS18B20]
  Q2 = MOSFET-NCHANNEL [package=to-92]
  Q4 = MOSFET-NCHANNEL [package=to-92]
  Q5 = MOSFET-NCHANNEL [package=to-92]
  R7 = Resistor [tolerance=±5% resistance=10k package=THT]
  R8 = Resistor [tolerance=±5% resistance=10k package=THT]
  R10 = Resistor [tolerance=±5% resistance=100 package=THT]
  R11 = Resistor [tolerance=±5% resistance=100 package=THT]
  Q6 = MOSFET-NCHANNEL [package=to-92]
  Q7 = MOSFET-NCHANNEL [package=to-92]
  Q8 = MOSFET-NCHANNEL [package=to-92]
  R12 = Resistor [tolerance=±5% resistance=10k package=THT]
  R13 = Resistor [tolerance=±5% resistance=10k package=THT]
  R14 = Resistor [tolerance=±5% resistance=10k package=THT]
  R15 = Resistor [tolerance=±5% resistance=100 package=THT]
  R16 = Resistor [tolerance=±5% resistance=100 package=THT]
  R17 = Resistor [tolerance=±5% resistance=100 package=THT]
  R5 = Resistor [tolerance=±5% resistance=100 package=THT]
  R20 = Resistor [tolerance=±5% resistance=100 package=THT]
  R21 = Resistor [tolerance=±5% resistance=10k package=THT]
  R22 = Resistor [tolerance=±5% resistance=10k package=THT]
  R23 = Resistor [tolerance=±5% resistance=4.7k package=THT]
  DS3 = DS18B20 1-Wire Temperature Sensor [part_number=DS18B20]
  DS4 = DS18B20 1-Wire Temperature Sensor [part_number=DS18B20]
  DS5 = DS18B20 1-Wire Temperature Sensor [part_number=DS18B20]
  RF_Jump = double row female pin header, 8 pins [form="♀ (female)"]
  GPS = female pin header, 6 pins [form="♀ (female)"]
  Compass = female pin header, 5 pins [form="♀ (female)"]
  GPS_Comms = female pin header, 5 pins [form="♀ (female)"]
  R25 = Resistor [tolerance=±5% resistance=10k package=THT]
  Photocell = female pin header, 2 pins [form="♀ (female)"]
  Accel = female pin header, 6 pins [form="♀ (female)"]
  Current_Bat = female pin header, 3 pins [form="♀ (female)"]
  Current_Sol = female pin header, 3 pins [form="♀ (female)"]
  Current_Left = female pin header, 3 pins [form="♀ (female)"]
  Current_Right = female pin header, 3 pins [form="♀ (female)"]
  Current_Center = female pin header, 3 pins [form="♀ (female)"]
  CRL_PWM = female pin header, 4 pins [form="♀ (female)"]
  RTC = Real Time Clock Module - DS1307 RTC Breakout Board
  R9 = Resistor [tolerance=±5% resistance=100 package=THT]
  R6 = Resistor [tolerance=±5% resistance=10k package=THT]
  Q3 = MOSFET-NCHANNEL [package=to-92]
  R29 = Resistor [tolerance=±5% resistance=100 package=THT]
  R30 = Resistor [tolerance=±5% resistance=100 package=THT]
  R31 = Resistor [tolerance=±5% resistance=100 package=THT]
  LED = female pin header, 2 pins [form="♀ (female)"]
  R32 = Resistor [tolerance=±5% resistance=100 package=THT]
  RLRC_FET = female pin header, 4 pins [form="♀ (female)"]

nets:
  N1: Part1.A11, Current_Center.pin3
  N2: Part1.A12, Current_Right.pin3
  N3: Part1.A13, Current_Left.pin3
  N4: Part1.A14, Current_Sol.pin3
  N5: Part1.A15, Current_Bat.pin3
  N6: Part1.A2, Accel.pin1
  N7: Part1.A3, Accel.pin2
  N8: Part1.A4, Accel.pin3
  N9: Part1.A5, R25.Pin_0
  N10: Part1.D21/SCL, Part1.SCL, Compass.pin3, RTC.SCL
  N11: Part1.D20/SDA, Part1.SDA, Compass.pin2, RTC.SDA
  N12: Part1.D17_PWM/RX2, GPS_Comms.pin4
  N13: Part1.D16_PWM/TX2, GPS_Comms.pin3
  N14: Part1.D15/RX3, GPS.pin4
  N15: Part1.D14/TX3, GPS.pin3
  N16: Part1.GND, Q1.G, Q2.G, Q4.G, Q5.G, R7.Pin_1, R8.Pin_1, Q6.G, Q7.G, Q8.G, R12.Pin_1, R13.Pin_1, R14.Pin_1, R21.Pin_1, R22.Pin_1, GPS_Comms.pin2, R25.Pin_1, CRL_PWM.pin1, R6.Pin_1, Q3.G
  VDD: Part1.5V, DS2.VDD, R23.Pin_0, DS3.VDD, DS4.VDD, DS5.VDD, RF_Jump.pin1, GPS.pin5, GPS_Comms.pin1, Photocell.pin2, Accel.pin6, Current_Bat.pin2, Current_Sol.pin2, Current_Left.pin2, Current_Right.pin2, Current_Center.pin2, RTC.5V, LED.pin1
  N17: Part1.D2_PWM, DS2.DQ, R23.Pin_1, DS3.DQ, DS4.DQ, DS5.DQ
  N18: Part1.D4_PWM, CRL_PWM.pin4
  N19: Part1.D5_PWM, CRL_PWM.pin3
  N20: Part1.D6_PWM, R5.Pin_0
  N21: Part1.D7_PWM, CRL_PWM.pin2
  N22: Part1.D22, GPS_Comms.pin5
  N23: Part1.D27, R15.Pin_0
  N24: Part1.D31, R32.Pin_0
  N25: Part1.D32, R11.Pin_0
  N26: Part1.D33, R31.Pin_0
  N27: Part1.D35, R29.Pin_0
  N28: Part1.D37, R30.Pin_0
  N29: Part1.D38, R20.Pin_0
  N30: Part1.D39, R9.Pin_0
  N31: Part1.D42, R16.Pin_0
  N32: Part1.D46, R17.Pin_0
  N33: Part1.D47, R10.Pin_0
  N34: Part1.D49, RF_Jump.pin7
  N35: Part1.D50, RF_Jump.pin5
  N36: Part1.D51, RF_Jump.pin3
  N37: Part1.D52, RF_Jump.pin6
  N38: Part1.D53, RF_Jump.pin2
  N39: Q1.D, R20.Pin_1, R22.Pin_0
  N40: Q1.S, RTC.GND
  GND: DS2.GND, Q2.S, DS3.GND, DS4.GND, DS5.GND
  N41: Q2.D, R5.Pin_1, R21.Pin_0
  N42: Q4.D, R7.Pin_0, R10.Pin_1
  N43: Q4.S, RF_Jump.pin8
  N44: Q5.D, R8.Pin_0, R11.Pin_1
  N45: Q5.S, Accel.pin4
  N46: Q6.D, R12.Pin_0, R15.Pin_1
  N47: Q6.S, GPS.pin2
  N48: Q7.D, R13.Pin_0, R16.Pin_1
  N49: Q7.S, Photocell.pin1
  N50: Q8.D, R14.Pin_0, R17.Pin_1
  N51: Q8.S, Current_Bat.pin1, Current_Sol.pin1, Current_Left.pin1, Current_Right.pin1, Current_Center.pin1
  N52: R9.Pin_1, R6.Pin_0, Q3.D
  N53: Q3.S, LED.pin2
  N54: R29.Pin_1, RLRC_FET.pin2
  N55: R30.Pin_1, RLRC_FET.pin1
  N56: R31.Pin_1, RLRC_FET.pin3
  N57: R32.Pin_1, RLRC_FET.pin4
